// Logisim project lab10.circ as structural Verilog: 1 circuit, main circuit main
module main (
  input  Clear,
  output A,
  output B
);

  wire clock_1_out, or_1_out;

  Clock #(.highDuration(1), .lowDuration(1)) clock_1 (.out(clock_1_out));
  or or_1 (or_1_out, A, B);
  J_K_Flip_Flop #(.trigger("rising")) j_k_ff_1 (
    .J(or_1_out), .clk(clock_1_out), .K(1'b0), .Q(A), .en(1'b1), .reset(Clear));  // open: Qn, preset
  J_K_Flip_Flop #(.trigger("rising")) j_k_ff_2 (
    .J(1'b1), .clk(clock_1_out), .K(or_1_out), .Q(B), .en(1'b1), .reset(Clear));  // open: Qn, preset
endmodule
